# Fritzing sketch BombDefuse (saved by Fritzing 0.9.3b)
breadboards: 2

parts:
  Composant1 = Arduino Uno (Rev3)
  R1 = Rotary Potentiometer (Large) [maximum_resistance=100kΩ package=THT]
  S1 = Toggle Switch [package=THT]
  R2 = Resistor [tolerance=±5% resistance=10k package=THT]
  U1 = mystery part, 2 pins [chip_label=Key]
  R3 = Resistor [tolerance=±5% resistance=10k package=THT]
  U2 = mystery part, 8 pins [chip_label=Keypad]
  LED1 = LED - 5mm [color="Red (633nm)" package="5 mm [THT]"]
  R4 = Resistor [tolerance=±5% resistance=220 package=THT]
  U3 = mystery part, 4 pins [chip_label=OLED]
  R5 = Resistor [tolerance=±5% resistance=220 package=THT]
  J1 = Piezo Speaker

nets:
  N1: Composant1.A0, R1.wiper
  N2: Composant1.A4/SDA, U3.pin4
  N3: Composant1.A5/SCL, U3.pin3
  N4: Composant1.D8, U2.pin4
  N5: Composant1.D9_PWM, U2.pin3
  N6: Composant1.D10_PWM/SS, U2.pin2
  N7: Composant1.D11_PWM/MOSI, U2.pin1
  N8: Composant1.D12/MISO, Composant1.5V, S1.COM, R2.Pin_0, U1.pin1, U3.pin2
  N9: Composant1.D13/SCK, U1.pin2, R3.Pin_0
  N10: Composant1.D2, R5.Pin_1
  N11: Composant1.D3_PWM, R4.Pin_1
  N12: Composant1.D4, U2.pin8
  N13: Composant1.D5_PWM, U2.pin7
  N14: Composant1.D6_PWM, U2.pin6
  N15: Composant1.D7, U2.pin5
  N16: Composant1.GND, R1.leg2, R2.Pin_1, R3.Pin_1, LED1.cathode, U3.pin1, J1.pin1
  N17: R1.leg1, S1.L2
  N18: LED1.anode, R4.Pin_0
  N19: R5.Pin_0, J1.pin2
